// Logisim project 7 segemnt display.circ as structural Verilog: 2 circuits, main circuit main
module main (
  input  b,
  input  d,
  input  a,
  input  c,
  output out_5,
  output out_6,
  output out_7,
  output out_8,
  output out_9,
  output out_10,
  output out_11
);

  wire and_1_out, and_2_out, and_3_out, and_4_out, and_5_out, and_6_out, and_7_out, and_8_out, and_9_out,
       and_10_out, and_11_out, and_12_out, and_13_out, and_14_out, and_15_out, and_16_out, and_17_out,
       and_18_out, and_19_out, and_20_out, and_21_out, and_22_out, and_23_out, and_24_out, and_25_out,
       and_26_out, and_27_out, and_28_out, and_29_out, and_30_out, and_31_out, and_32_out, and_33_out,
       and_34_out, not_1_out, not_2_out, not_3_out, not_4_out, xor_1_out, xor_2_out;

  not not_1 (not_1_out, a);
  not not_2 (not_2_out, b);
  not not_3 (not_3_out, c);
  not not_4 (not_4_out, d);
  xor xor_1 (xor_1_out, a, b);
  and and_1 (and_1_out, not_3_out, d);
  and and_2 (and_2_out, not_1_out, not_3_out);
  and and_3 (and_3_out, not_1_out, d);
  and and_4 (and_4_out, a, not_3_out);
  xor xor_2 (xor_2_out, d, b);
  and and_5 (and_5_out, not_1_out, b, not_3_out, d);
  and and_6 (and_6_out, not_4_out, not_1_out, not_2_out);
  and and_7 (and_7_out, a, b);
  and and_8 (and_8_out, c, not_4_out);
  and and_9 (and_9_out, a, c);
  and and_10 (and_10_out, not_2_out, not_4_out);
  and and_11 (and_11_out, c, not_4_out);
  and and_12 (and_12_out, a, not_2_out);
  and and_13 (and_13_out, a, d);
  and and_14 (and_14_out, not_1_out, b, not_3_out);
  and and_15 (and_15_out, c, d, not_2_out);
  and and_16 (and_16_out, not_3_out, not_4_out);
  and and_17 (and_17_out, a, not_2_out);
  and and_18 (and_18_out, a, c);
  and and_19 (and_19_out, b, c, not_4_out);
  and and_20 (and_20_out, not_1_out, b);
  and and_21 (and_21_out, c, not_4_out);
  and and_22 (and_22_out, c, b);
  and and_23 (and_23_out, not_4_out, not_2_out);
  and and_24 (and_24_out, a, not_4_out);
  and and_25 (and_25_out, a, not_2_out, not_3_out);
  and and_26 (and_26_out, not_1_out, b, d);
  and and_27 (and_27_out, c, not_1_out);
  and and_28 (and_28_out, not_1_out, not_2_out);
  and and_29 (and_29_out, not_2_out, not_3_out);
  and and_30 (and_30_out, not_4_out, not_2_out);
  and and_31 (and_31_out, c, d, not_1_out);
  and and_32 (and_32_out, not_3_out, not_4_out, not_1_out);
  and and_33 (and_33_out, a, not_3_out, d);
  and and_34 (and_34_out, c, xor_2_out);
  or or_1 (out_5, xor_1_out, and_1_out, and_2_out, and_3_out);
  or or_2 (out_7, and_7_out, and_8_out, and_9_out, and_10_out);
  or or_3 (out_8, and_11_out, and_12_out, and_15_out, and_13_out, and_14_out);
  or or_4 (out_9, and_16_out, and_17_out, and_20_out, and_18_out, and_19_out);
  or or_5 (out_10, and_25_out, and_21_out, and_22_out, and_27_out, and_23_out, and_24_out, and_26_out);
  or or_6 (out_11, and_32_out, and_28_out, and_29_out, and_30_out, and_31_out, and_33_out);
  or or_7 (out_6, and_4_out, and_34_out, and_5_out, and_6_out);
  _7_Segment_Display u_7_segment_display_1 (
    .g(out_8), .f(out_9), .a(out_10), .b(out_11), .e(out_7), .d(out_6), .c(out_5));  // open: dp

  // Notes on the sheet:
  //   a
  //   b
  //   c
  //   d
  //   A XOR B
  //   C'D
  //   A'C'
  //   A'D
  //   AB
  //   CD'
  //   AC
  //   B'D'
  //   CD'
  //   AD
  //   A'BC'
  //   B'CD
  //   C'D'
  //   AB'
  //   AC
  //   BCD'
  //   CD'
  //   B'D'
  //   AB'C'
  //   A'C
  //   A'B'
  //   B'C'
  //   B'D'
  //   A'C
  //   C(B XOR D)
  //   A'BC'D
  //   A'B'D'
  //   AB'
  //   A'B
  //   CB
  //   AD'
  //   A'BD
  //   A'CD
  //   A'C'D'
  //   AC'D
endmodule

module CIRCUIT (
  input  in_1,
  input  in_2,
  input  in_3,
  input  in_4
);

  wire main_1_out_5, main_1_out_6, main_1_out_7, main_1_out_8, main_1_out_9, main_1_out_10, main_1_out_11;

  main main_1 (
    .out_5(main_1_out_5), .out_6(main_1_out_6), .out_7(main_1_out_7), .out_8(main_1_out_8),
    .out_9(main_1_out_9), .out_10(main_1_out_10), .a(in_1), .b(in_2), .c(in_3), .d(in_4),
    .out_11(main_1_out_11));
  _7_Segment_Display u_7_segment_display_1 (
    .g(main_1_out_8), .f(main_1_out_9), .a(main_1_out_10), .b(main_1_out_11), .e(main_1_out_7),
    .d(main_1_out_6), .c(main_1_out_5));  // open: dp
endmodule
